// Logisim project cachemem.circ as structural Verilog: 2 circuits, main circuit main
module main (
  output [7:0] dataout
);

  wire button_1_out, clock_1_out, not_1_out;
  wire [7:0] counter_1_q;
  wire [15:0] rom_1_data;

  Clock clock_1 (.out(clock_1_out));
  Button button_1 (.out(button_1_out));
  Counter counter_1 (.Q(counter_1_q), .clk(clock_1_out), .clr(button_1_out));  // open: load, D, count, carry
  ROM #(.dataWidth(16)) rom_1 (.addr(counter_1_q), .data(rom_1_data), .sel(1'b1));
  memorysystem memorysystem_1 (
    .addr({4'b0000, rom_1_data[11:0]}), .datain(rom_1_data[14:12]), .Clock(clock_1_out),
    .Write(rom_1_data[15]), .Read(not_1_out), .dataout(dataout));  // open: Reset, out_8
  not not_1 (not_1_out, rom_1_data[15]);
  Hex_Digit_Display hex_digit_display_1 (.value(dataout[7:4]));  // open: dp
  Hex_Digit_Display hex_digit_display_2 (.value(dataout[3:0]));  // open: dp

  // Notes on the sheet:
  //   Fake instructions
  //   R/W bit plus mem addresses
  //   Leading bit... 0=R, 1=W
  //   contents of rom_1 (hex, n*v repeats v):
  //   0 1 2 3 4 5 6 7 8008 8009 800a 800b 800c 800d 800e 800f
endmodule

module memorysystem (
  input  [15:0] addr,
  input  [2:0] datain,
  input  Clock,
  input  Write,
  input  Read,
  input  Reset,
  output [7:0] dataout,
  output [31:0] out_8
);

  wire and_1_out, comparator_1_eq, comparator_2_eq, HitDetector_out, not_1_out, not_2_out;
  wire [3:0] BC;
  wire [7:0] ram_4_data;
  wire [10:0] ram_1_data;

  not not_1 (not_1_out, comparator_1_eq);
  Comparator #(.width(4)) comparator_1 (.a(BC), .b(4'b0000), .eq(comparator_1_eq));  // open: gt, lt
  and and_1 (and_1_out, comparator_1_eq, Clock);
  Counter HitCounter (.count(HitDetector_out), .clk(and_1_out), .clr(Reset));  // open: load, D, Q, carry
  RAM #(.addrWidth(2), .dataWidth(11), .bus("separate")) ram_1 (
    .addr(addr[5:4]), .din({1'b1, addr[15:6]}), .data(ram_1_data), .str(not_1_out), .sel(1'b1), .clk(Clock),
    .ld(comparator_1_eq), .clr(Reset));
  Counter MissCounter (.count(not_2_out), .clk(and_1_out), .clr(Reset));  // open: load, D, Q, carry
  not not_2 (not_2_out, HitDetector_out);
  and HitDetector (HitDetector_out, ram_1_data[10], comparator_1_eq, comparator_2_eq);
  RAM #(.addrWidth(2), .dataWidth(32), .bus("separate")) ram_2 (
    .addr(addr[5:4]), .din(out_8), .str(not_1_out), .clk(Clock), .clr(Reset));  // open: data, sel, ld
  Comparator #(.width(10)) comparator_2 (.a(ram_1_data[9:0]), .b(addr[15:6]), .eq(comparator_2_eq));  // open: gt, lt
  RAM #(.addrWidth(2), .dataWidth(32), .bus("separate")) ram_3 (
    .addr(addr[5:4]), .din(out_8), .str(not_1_out), .clk(Clock), .clr(Reset));  // open: data, sel, ld
  Counter #(.width(4), .max('hf)) counter_1 (.Q(BC), .clk(Clock), .clr(Reset));  // open: load, D, count, carry
  RAM #(.addrWidth(16), .bus("separate")) ram_4 (
    .addr({addr[15:4], BC}), .din({{5{1'b0}}, datain}), .data(ram_4_data), .str(Write), .sel(1'b1),
    .clk(Clock), .ld(Read), .clr(Reset));
  Shift_Register #(.width(8), .length(4)) shift_register_1 (
    .shift(1'b1), .in(ram_4_data), .clk(Clock), .q0(out_8[31:24]), .q1(out_8[23:16]), .q2(out_8[15:8]),
    .q3(out_8[7:0]));  // open: out, load, clr, d0, d1, d2, d3
  RAM #(.addrWidth(2), .dataWidth(32), .bus("separate")) ram_5 (
    .addr(addr[5:4]), .din(out_8), .str(not_1_out), .clk(Clock), .clr(Reset));  // open: data, sel, ld
  RAM #(.addrWidth(2), .dataWidth(32), .bus("separate")) ram_6 (
    .addr(addr[5:4]), .din(out_8), .str(not_1_out), .clk(Clock), .clr(Reset));  // open: data, sel, ld

  // Notes on the sheet:
  //   Metadata (tag and valid bits)
  //   Cache with block size of 16 bytes and a tiny one at that with only FOUR cache lines
  //   RAM
endmodule
